// Logisim project aulaFlipFlops.circ as structural Verilog: 1 circuit, main circuit main
module main (
  input  S_C,
  input  S_O,
  input  S_P,
  output M_ON,
  output M_CLOSE,
  output NS1,
  output NS0,
  output AS1,
  output AS0
);

  wire clock_1_out;

  Clock clock_1 (.out(clock_1_out));
  // PLD #(.Contents("{\"version\":\"1.0\",\"deviceId\":\"v750c\",\"file\":\"aulaFlipFlops.doc\",\"variables\":{\"MCLK\":false,\"AS1.dfb\":false,\"S_O\":false,\"AS0.dfb\":false,\"M_ON\":false,\"S_P\":false,\"S_C\":false,\"M_CLOSE\":false,\"NS0\":false,\"NS1\":false,\"AS0\":false,\"AS1\":false},\"productTerms\":[{\"type\":\"X\",\"pin\":14,\"result\":false,\"name\":\"AS0.d\",\"expression\":\"NS0\"},{\"type\":\"X\",\"pin\":14,\"name\":\"AS0.ar\",\"expression\":\"0\"},{\"type\":\"X\",\"pin\":14,\"name\":\"AS0.ckmux\",\"expression\":\"MCLK\"},{\"type\":\"X\",\"pin\":14,\"name\":\"AS0.sp\",\"expression\":\"0\"},{\"type\":\"X\",\"pin\":15,\"name\":\"AS1.d\",\"expression\":\"NS1\"},{\"type\":\"X\",\"pin\":15,\"name\":\"AS1.ar\",\"expression\":\"0\"},{\"type\":\"X\",\"pin\":15,\"name\":\"AS1.ckmux\",\"expression\":\"MCLK\"},{\"type\":\"X\",\"pin\":15,\"name\":\"AS1.sp\",\"expression\":\"0\"},{\"type\":\"V\",\"pin\":20,\"name\":\"M_CLOSE\",\"expression\":\"AS0\\u0026!AS1\"},{\"type\":\"V\",\"pin\":21,\"name\":\"M_ON\",\"expression\":\"AS0\"},{\"type\":\"V\",\"pin\":17,\"name\":\"NS0\",\"expression\":\"!AS0\\u0026AS1\\u0026!S_C#AS0\\u0026!AS1\\u0026!S_C#AS0\\u0026AS1\\u0026!S_O#!AS0\\u0026AS1\\u0026S_P#AS0\\u0026!AS1\\u0026S_P#!AS0\\u0026!AS1\\u0026!S_P\"},{\"type\":\"V\",\"pin\":18,\"name\":\"NS1\",\"expression\":\"!AS0\\u0026AS1#AS1\\u0026!S_O#AS0\\u0026!AS1\\u0026S_C#AS0\\u0026!AS1\\u0026S_P\"},{\"type\":\"D\",\"pin\":14,\"name\":\"AS0.oe\",\"expression\":\"1\"},{\"type\":\"D\",\"pin\":15,\"name\":\"AS1.oe\",\"expression\":\"1\"},{\"type\":\"D\",\"pin\":20,\"name\":\"M_CLOSE.oe\",\"expression\":\"1\"},{\"type\":\"D\",\"pin\":21,\"name\":\"M_ON.oe\",\"expression\":\"1\"},{\"type\":\"D\",\"pin\":17,\"name\":\"NS0.oe\",\"expression\":\"1\"},{\"type\":\"D\",\"pin\":18,\"name\":\"NS1.oe\",\"expression\":\"1\"}],\"projectName\":\"aulaFlipFlops\",\"pins\":{\"1\":{\"termUsed\":\"-\",\"type\":\"V\",\"name\":\"MCLK\",\"number\":1,\"negated\":false,\"extensions\":{},\"fuseNot\":false},\"17\":{\"termUsed\":\"6\",\"type\":\"V\",\"name\":\"NS0\",\"number\":17,\"negated\":false,\"extensions\":{\"oe\":false},\"fuseNot\":false},\"18\":{\"termUsed\":\"4\",\"type\":\"V\",\"name\":\"NS1\",\"number\":18,\"negated\":false,\"extensions\":{\"oe\":false},\"fuseNot\":false},\"3\":{\"termUsed\":\"-\",\"type\":\"V\",\"name\":\"S_C\",\"number\":3,\"negated\":false,\"extensions\":{},\"fuseNot\":false},\"20\":{\"termUsed\":\"1\",\"type\":\"V\",\"name\":\"M_CLOSE\",\"number\":20,\"negated\":false,\"extensions\":{\"oe\":false},\"fuseNot\":false},\"21\":{\"termUsed\":\"1\",\"type\":\"V\",\"name\":\"M_ON\",\"number\":21,\"negated\":false,\"extensions\":{\"oe\":false},\"fuseNot\":false},\"5\":{\"termUsed\":\"-\",\"type\":\"V\",\"name\":\"S_O\",\"number\":5,\"negated\":false,\"extensions\":{},\"fuseNot\":false},\"7\":{\"termUsed\":\"-\",\"type\":\"V\",\"name\":\"S_P\",\"number\":7,\"negated\":false,\"extensions\":{},\"fuseNot\":false},\"14\":{\"termUsed\":\"-\",\"type\":\"V\",\"name\":\"AS0\",\"number\":14,\"negated\":false,\"extensions\":{\"ar\":false,\"d\":false,\"oe\":false,\"ckmux\":false,\"sp\":false},\"fuseNot\":false},\"15\":{\"termUsed\":\"-\",\"type\":\"V\",\"name\":\"AS1\",\"number\":15,\"negated\":false,\"extensions\":{\"ar\":false,\"d\":false,\"oe\":false,\"ckmux\":false,\"sp\":false},\"fuseNot\":false}}}")) pld_1: pin names not known; wires that end beside it: clock_1_out, S_C, S_O, S_P, M_ON, M_CLOSE, NS1, NS0, AS1, AS0
endmodule
