// Logisim project LEETC_LSD_Trabalho_1_2023_24_v2.circ as structural Verilog: 5 circuits, main circuit Testador
module Testador (
  input  A,
  input  B,
  input  F1,
  input  F2,
  input  F3,
  input  FR,
  output OK,
  output FSEL
);

  wire codificador_1_y0, codificador_1_y1, \geradorfunção_1_r ;

  Codificador codificador_1 (.I0(F1), .I1(F2), .I2(F3), .Y0(codificador_1_y0), .Y1(codificador_1_y1), .FS(FSEL));
  \GeradorFunção  \geradorfunção_1  (
    .C0(A), .C1(B), .FC0(codificador_1_y0), .FC1(codificador_1_y1), .R(\geradorfunção_1_r ));
  Validador validador_1 (.RG(\geradorfunção_1_r ), .E(FSEL), .V(OK), .RR(FR));
endmodule

module Codificador (
  input  I0,
  input  I1,
  input  I2,
  output Y0,
  output Y1,
  output FS
);

  wire and_1_out;

  and and_1 (and_1_out, I0, ~I1, ~I2);  // AND_Gate
  or or_1 (Y0, and_1_out, I2);
  or or_2 (Y1, I2, I1);
  or or_3 (FS, I0, I1, I2);
endmodule

module \GeradorFunção  (
  input  C0,
  input  C1,
  input  FC0,
  input  FC1,
  output R
);

  wire and_1_out, and_2_out, and_3_out, and_4_out, and_5_out;

  and and_1 (and_1_out, ~C1, FC0, ~FC1);  // AND_Gate
  and and_2 (and_2_out, C0, ~C1, FC0);  // AND_Gate
  and and_3 (and_3_out, ~C0, C1, FC0);  // AND_Gate
  and and_4 (and_4_out, ~C0, ~FC0, FC1);  // AND_Gate
  and and_5 (and_5_out, C1, ~FC0, FC1);  // AND_Gate
  or or_1 (R, and_1_out, and_2_out, and_3_out, and_4_out, and_5_out);
endmodule

module Validador (
  input  E,
  input  RG,
  input  RR,
  output V
);

  wire and_1_out, and_2_out, or_1_out;

  and and_1 (and_1_out, RG, RR);
  and and_2 (and_2_out, ~RG, ~RR);  // AND_Gate
  or or_1 (or_1_out, and_1_out, and_2_out);
  and and_3 (V, E, or_1_out);
endmodule

module Testador_com_PAL (
  input  A,
  input  B,
  input  F1,
  input  F2,
  input  F3,
  input  FR,
  output OK,
  output FSEL
);

  // PLD #(.Contents("{\"version\":\"1.0\",\"deviceId\":\"v750c\",\"file\":\"trab1.doc\",\"variables\":{},\"productTerms\":[{\"type\":\"I\",\"pin\":0,\"name\":\"C0\",\"expression\":\"A\"},{\"type\":\"I\",\"pin\":0,\"name\":\"C1\",\"expression\":\"B\"},{\"type\":\"I\",\"pin\":0,\"name\":\"E\",\"expression\":\"F1#F2#F3\"},{\"type\":\"I\",\"pin\":0,\"name\":\"FC0\",\"expression\":\"F3#F1\\u0026!F2\\u0026!F3\"},{\"type\":\"I\",\"pin\":0,\"name\":\"FC1\",\"expression\":\"F2#F3\"},{\"type\":\"I\",\"pin\":0,\"name\":\"FS\",\"expression\":\"F1#F2#F3\"},{\"type\":\"V\",\"pin\":14,\"name\":\"FSEL\",\"expression\":\"F1#F2#F3\"},{\"type\":\"V\",\"pin\":18,\"name\":\"OK\",\"expression\":\"!A\\u0026B\\u0026F3\\u0026FR#A\\u0026!B\\u0026F3\\u0026FR#!A\\u0026F1\\u0026!F3\\u0026FR#!A\\u0026F2\\u0026!F3\\u0026FR#B\\u0026F2\\u0026!F3\\u0026FR#A\\u0026B\\u0026F3\\u0026!FR#!A\\u0026!B\\u0026F3\\u0026!FR#A\\u0026!B\\u0026F1\\u0026!F2\\u0026FR#A\\u0026B\\u0026F1\\u0026!F2\\u0026!FR#A\\u0026!B\\u0026F2\\u0026!F3\\u0026!FR\"},{\"type\":\"I\",\"pin\":0,\"name\":\"R\",\"expression\":\"B\\u0026F2\\u0026!F3#!A\\u0026B\\u0026F3#!A\\u0026B\\u0026F1\\u0026!F2\\u0026!F3#!A\\u0026F2\\u0026!F3#!B\\u0026F1\\u0026!F2\\u0026!F3#A\\u0026!B\\u0026F3\"},{\"type\":\"I\",\"pin\":0,\"name\":\"RG\",\"expression\":\"B\\u0026F2\\u0026!F3#!A\\u0026B\\u0026F3#!A\\u0026B\\u0026F1\\u0026!F2\\u0026!F3#!A\\u0026F2\\u0026!F3#!B\\u0026F1\\u0026!F2\\u0026!F3#A\\u0026!B\\u0026F3\"},{\"type\":\"I\",\"pin\":0,\"name\":\"RR\",\"expression\":\"FR\"},{\"type\":\"I\",\"pin\":0,\"name\":\"V\",\"expression\":\"!A\\u0026!B\\u0026F3\\u0026!FR#A\\u0026B\\u0026F1\\u0026!F2\\u0026!F3\\u0026!FR#A\\u0026B\\u0026F3\\u0026!FR#A\\u0026!B\\u0026F2\\u0026!F3\\u0026!FR#B\\u0026F2\\u0026!F3\\u0026FR#!A\\u0026F2\\u0026!F3\\u0026FR#!B\\u0026F1\\u0026!F2\\u0026!F3\\u0026FR#A\\u0026!B\\u0026F3\\u0026FR#!A\\u0026B\\u0026F3\\u0026FR#!A\\u0026B\\u0026F1\\u0026!F2\\u0026!F3\\u0026FR\"},{\"type\":\"I\",\"pin\":0,\"name\":\"Y0\",\"expression\":\"F3#F1\\u0026!F2\\u0026!F3\"},{\"type\":\"I\",\"pin\":0,\"name\":\"Y1\",\"expression\":\"F2#F3\"},{\"type\":\"D\",\"pin\":14,\"name\":\"FSEL.oe\",\"expression\":\"1\"},{\"type\":\"D\",\"pin\":18,\"name\":\"OK.oe\",\"expression\":\"1\"}],\"projectName\":\"TP1\",\"pins\":{\"1\":{\"termUsed\":\"-\",\"type\":\"V\",\"name\":\"A\",\"number\":1,\"negated\":false,\"extensions\":{},\"fuseNot\":false},\"2\":{\"termUsed\":\"-\",\"type\":\"V\",\"name\":\"B\",\"number\":2,\"negated\":false,\"extensions\":{},\"fuseNot\":false},\"18\":{\"termUsed\":\"10\",\"type\":\"V\",\"name\":\"OK\",\"number\":18,\"negated\":false,\"extensions\":{\"oe\":false},\"fuseNot\":false},\"3\":{\"termUsed\":\"-\",\"type\":\"V\",\"name\":\"F1\",\"number\":3,\"negated\":false,\"extensions\":{},\"fuseNot\":false},\"4\":{\"termUsed\":\"-\",\"type\":\"V\",\"name\":\"F2\",\"number\":4,\"negated\":false,\"extensions\":{},\"fuseNot\":false},\"5\":{\"termUsed\":\"-\",\"type\":\"V\",\"name\":\"F3\",\"number\":5,\"negated\":false,\"extensions\":{},\"fuseNot\":false},\"6\":{\"termUsed\":\"-\",\"type\":\"V\",\"name\":\"FR\",\"number\":6,\"negated\":false,\"extensions\":{},\"fuseNot\":false},\"14\":{\"termUsed\":\"3\",\"type\":\"V\",\"name\":\"FSEL\",\"number\":14,\"negated\":false,\"extensions\":{\"oe\":false},\"fuseNot\":false}}}")) pld_1: pin names not known; wires that end beside it: A, B, F1, F2, F3, FR, OK, FSEL
endmodule
