// Logisim project gerador_funcao.circ as structural Verilog: 1 circuit, main circuit main
module main (
  input  C0,
  input  C1,
  input  FC0,
  input  FC1,
  output OK
);

  wire and_1_out, and_2_out, and_3_out, and_4_out, and_5_out;

  and and_1 (and_1_out, ~C1, FC0, ~FC1);  // AND_Gate
  and and_2 (and_2_out, C0, ~C1, FC0);  // AND_Gate
  and and_3 (and_3_out, ~C0, C1, FC0);  // AND_Gate
  and and_4 (and_4_out, ~C0, ~FC0, FC1);  // AND_Gate
  and and_5 (and_5_out, C1, ~FC0, FC1);  // AND_Gate
  or or_1 (OK, and_1_out, and_2_out, and_3_out, and_4_out, and_5_out);

  // Notes on the sheet:
  //   1
  //   5
endmodule
