// Logisim project priorityencoder.circ as structural Verilog: 1 circuit, main circuit main
module main (
  input  F1,
  input  F2,
  input  F3,
  output Y0,
  output Y1,
  output FS
);

  wire and_1_out;

  and and_1 (and_1_out, F1, ~F2, ~F3);  // AND_Gate
  or or_1 (Y0, and_1_out, F3);
  or or_2 (Y1, F3, F2);
  or or_3 (FS, F1, F2, F3);
endmodule
