// Logisim project validador.circ as structural Verilog: 1 circuit, main circuit main
module main (
  input  E,
  input  RG,
  input  RR,
  output OK
);

  wire and_1_out, and_2_out, or_1_out;

  and and_1 (and_1_out, RG, RR);
  and and_2 (and_2_out, ~RG, ~RR);  // AND_Gate
  or or_1 (or_1_out, and_1_out, and_2_out);
  and and_3 (OK, E, or_1_out);
endmodule
