// Logisim project LEETC_LSD_Trabalho_2_2023_24.circ as structural Verilog: 18 circuits, main circuit Aritmetico
module main (
  input  A3,
  input  in_2,
  input  in_3,
  input  A0,
  input  B3,
  input  in_6,
  input  in_7,
  input  B0,
  input  CyBwi,
  input  S2,
  input  S1,
  input  S0,
  output R0,
  output out_14,
  output out_15,
  output R3,
  output LE,
  output V,
  output CyBwo
);

  ALU alu_1 (
    .CyBwi(CyBwi), .A0(A0), .A1(in_3), .A2(in_2), .A3(A3), .B0(B0), .B1(in_7), .B2(in_6), .B3(B3), .S1(S1),
    .S2(S2), .R0(R0), .R1(out_14), .R2(out_15), .R3(R3), .V(V), .LE(LE), .CyBwo(CyBwo), .S0(S0));
endmodule

module ALU (
  input  CyBwi,
  input  A0,
  input  A1,
  input  A2,
  input  A3,
  input  B0,
  input  B1,
  input  B2,
  input  B3,
  input  S0,
  input  S1,
  input  S2,
  output R0,
  output R1,
  output R2,
  output R3,
  output LE,
  output V,
  output CyBwo
);

  wire aritmetico_1_a3_2, aritmetico_1_bt3, aritmetico_1_cybwa, aritmetico_1_ra0, aritmetico_1_ra1,
       aritmetico_1_ra2, aritmetico_1_ra3, logicoshift_1_lsl4, logicoshift_1_rlogic0, logicoshift_1_rlogic1,
       logicoshift_1_rlogic2, logicoshift_1_rlogic3;

  Aritmetico aritmetico_1 (
    .CyBwi(CyBwi), .A0(A0), .A1(A1), .A2(A2), .A3(A3), .B0(B0), .B1(B1), .B2(B2), .B3(B3), .OP1(S1),
    .RA0(aritmetico_1_ra0), .RA1(aritmetico_1_ra1), .RA2(aritmetico_1_ra2), .RA3(aritmetico_1_ra3),
    .CyBwA(aritmetico_1_cybwa), .A3_2(aritmetico_1_a3_2), .OP0(S0), .BT3(aritmetico_1_bt3));
  LogicoShift logicoshift_1 (
    .A0(A0), .A1(A1), .A2(A2), .A3(A3), .B0(B0), .B1(B1), .B2(B2), .B3(B3), .SnL(S0),
    .RLogic0(logicoshift_1_rlogic0), .RLogic1(logicoshift_1_rlogic1), .RLogic2(logicoshift_1_rlogic2),
    .RLogic3(logicoshift_1_rlogic3), .LSL4(logicoshift_1_lsl4));
  Mux_2x4 mux_2x4_1 (
    .a0(aritmetico_1_ra0), .b0(logicoshift_1_rlogic0), .a1(aritmetico_1_ra1), .b1(logicoshift_1_rlogic1),
    .a2(aritmetico_1_ra2), .b2(logicoshift_1_rlogic2), .a3(aritmetico_1_ra3), .b3(logicoshift_1_rlogic3),
    .S(S2), .y0(R0), .y1(R1), .y2(R2), .y3(R3));
  Flags flags_1 (
    .R0(R0), .R1(R1), .R2(R2), .R3(R3), .A3(aritmetico_1_a3_2), .BT3(aritmetico_1_bt3),
    .CyBwA(aritmetico_1_cybwa), .SHL4(logicoshift_1_lsl4), .OP0(S2), .LE(LE), .V(V), .CyBwo(CyBwo));
endmodule

module Aritmetico (
  input  CyBwi,
  input  A0,
  input  A1,
  input  A2,
  input  A3,
  input  B0,
  input  B1,
  input  B2,
  input  B3,
  input  OP1,
  input  OP0,
  output RA0,
  output RA1,
  output RA2,
  output RA3,
  output CyBwA,
  output A3_2,
  output BT3
);

  wire adder4bit_1_c4, btrans_1_bt0, btrans_1_bt1, btrans_1_bt2, cybw_1_c0;

  CyBw cybw_1 (.CyBwi(CyBwi), .S0(OP0), .S1(OP1), .C0(cybw_1_c0));
  BTrans btrans_1 (
    .B0(B0), .B1(B1), .B2(B2), .B3(B3), .BT0(btrans_1_bt0), .BT1(btrans_1_bt1), .BT2(btrans_1_bt2),
    .BT3(BT3), .C(OP0));
  Adder4bit adder4bit_1 (
    .C0(cybw_1_c0), .A0(A0), .B0(btrans_1_bt0), .A1(A1), .B1(btrans_1_bt1), .A2(A2), .B2(btrans_1_bt2),
    .A3(A3), .B3(BT3), .S0(RA0), .S1(RA1), .S2(RA2), .S3(RA3), .C4(adder4bit_1_c4));
  C4T c4t_1 (.C4(adder4bit_1_c4), .SnA(OP0), .CyBwA(CyBwA));

  assign A3_2 = A3;
endmodule

module LogicoShift (
  input  A0,
  input  A1,
  input  A2,
  input  A3,
  input  B0,
  input  B1,
  input  B2,
  input  B3,
  input  SnL,
  output RLogic0,
  output RLogic1,
  output RLogic2,
  output RLogic3,
  output LSL4
);

  wire logico_1_and0, logico_1_and1, logico_1_and2, logico_1_and3, logicshiftleft_1_lsl0,
       logicshiftleft_1_lsl1, logicshiftleft_1_lsl2, logicshiftleft_1_lsl3;

  Logico logico_1 (
    .A0(A0), .B0(B0), .A1(A1), .B1(B1), .A2(A2), .B2(B2), .A3(A3), .B3(B3), .AND0(logico_1_and0),
    .AND1(logico_1_and1), .AND2(logico_1_and2), .AND3(logico_1_and3));
  LogicShiftLeft logicshiftleft_1 (
    .A0(A0), .A1(A1), .A2(A2), .A3(A3), .S1(B1), .S0(B0), .LSL0(logicshiftleft_1_lsl0),
    .LSL1(logicshiftleft_1_lsl1), .LSL2(logicshiftleft_1_lsl2), .LSL3(logicshiftleft_1_lsl3), .LSL4(LSL4));
  Mux_2x4 mux_2x4_1 (
    .a0(logico_1_and0), .b0(logicshiftleft_1_lsl0), .a1(logico_1_and1), .b1(logicshiftleft_1_lsl1),
    .a2(logico_1_and2), .b2(logicshiftleft_1_lsl2), .a3(logico_1_and3), .b3(logicshiftleft_1_lsl3), .S(SnL),
    .y0(RLogic0), .y1(RLogic1), .y2(RLogic2), .y3(RLogic3));
endmodule

module Flags (
  input  R0,
  input  R1,
  input  R2,
  input  R3,
  input  A3,
  input  BT3,
  input  CyBwA,
  input  SHL4,
  input  OP0,
  output LE,
  output V,
  output CyBwo
);

  wire and_1_out;

  and and_1 (and_1_out, ~R0, ~R1, ~R2, ~R3);  // AND_Gate
  overflaw overflaw_1 (.A3(A3), .B3(BT3), .R3(R3), .OV(V));
  LE le_1 (.Z(and_1_out), .R3(R3), .V(V), .LTE(LE));
  Mux_2x1 mux_2x1_1 (.I0(CyBwA), .I1(SHL4), .S(OP0), .Y(CyBwo));  // open: out_5
endmodule

module Adder4bit (
  input  C0,
  input  A0,
  input  B0,
  input  A1,
  input  B1,
  input  A2,
  input  B2,
  input  A3,
  input  B3,
  output S0,
  output S1,
  output S2,
  output S3,
  output C4
);

  wire fulladder_1_ci_1, fulladder_2_ci_1, fulladder_3_ci_1;

  FullAdder fulladder_1 (.ai(A0), .bi(B0), .ci(C0), .si(S0), .ci_1(fulladder_1_ci_1));
  FullAdder fulladder_2 (.ai(A1), .bi(B1), .ci(fulladder_1_ci_1), .si(S1), .ci_1(fulladder_2_ci_1));
  FullAdder fulladder_3 (.ai(A2), .bi(B2), .ci(fulladder_2_ci_1), .si(S2), .ci_1(fulladder_3_ci_1));
  FullAdder fulladder_4 (.ai(A3), .bi(B3), .ci(fulladder_3_ci_1), .si(S3), .ci_1(C4));
endmodule

module FullAdder (
  input  ai,
  input  bi,
  input  ci,
  output si,
  output ci_1
);

  wire and_1_out, and_2_out, and_3_out;

  and and_1 (and_1_out, ai, bi);
  and and_2 (and_2_out, ai, ci);
  and and_3 (and_3_out, bi, ci);
  xor xor_1 (si, ai, bi, ci);
  or or_1 (ci_1, and_1_out, and_2_out, and_3_out);
endmodule

module overflaw (
  input  A3,
  input  B3,
  input  R3,
  output OV
);

  wire and_1_out, and_2_out;

  and and_1 (and_1_out, A3, B3, ~R3);  // AND_Gate
  and and_2 (and_2_out, ~A3, ~B3, R3);  // AND_Gate
  or or_1 (OV, and_1_out, and_2_out);
endmodule

module LE (
  input  Z,
  input  R3,
  input  V,
  output LTE
);

  wire xor_1_out;

  xor xor_1 (xor_1_out, R3, V);
  or or_1 (LTE, Z, xor_1_out);
endmodule

module Logico (
  input  A0,
  input  B0,
  input  A1,
  input  B1,
  input  A2,
  input  B2,
  input  A3,
  input  B3,
  output AND0,
  output AND1,
  output AND2,
  output AND3
);

  and and_1 (AND0, A0, B0);
  and and_2 (AND1, A1, B1);
  and and_3 (AND2, A2, B2);
  and and_4 (AND3, A3, B3);
endmodule

module LogicShiftLeft (
  input  A0,
  input  A1,
  input  A2,
  input  A3,
  input  S1,
  input  S0,
  output LSL0,
  output LSL1,
  output LSL2,
  output LSL3,
  output LSL4
);

  wire mux_4x1_2_out_8, mux_4x1_2_out_9, mux_4x1_3_out_8, mux_4x1_3_out_9, mux_4x1_4_out_8, mux_4x1_4_out_9,
       mux_4x1_5_out_8, mux_4x1_5_out_9;

  Mux_4x1 mux_4x1_1 (
    .I0(A0), .I1(1'b0), .I2(1'b0), .I3(1'b0), .S0(mux_4x1_2_out_8), .S1(mux_4x1_2_out_9), .Y(LSL0));  // open: out_8, out_9
  Mux_4x1 mux_4x1_2 (
    .I0(A1), .I1(A0), .I2(1'b0), .I3(1'b0), .S0(mux_4x1_3_out_8), .S1(mux_4x1_3_out_9), .Y(LSL1),
    .out_8(mux_4x1_2_out_8), .out_9(mux_4x1_2_out_9));
  Mux_4x1 mux_4x1_3 (
    .I0(A2), .I1(A1), .I2(A0), .I3(1'b0), .S0(mux_4x1_4_out_8), .S1(mux_4x1_4_out_9), .Y(LSL2),
    .out_8(mux_4x1_3_out_8), .out_9(mux_4x1_3_out_9));
  Mux_4x1 mux_4x1_4 (
    .I0(A3), .I1(A2), .I2(A1), .I3(A0), .S0(mux_4x1_5_out_8), .S1(mux_4x1_5_out_9), .Y(LSL3),
    .out_8(mux_4x1_4_out_8), .out_9(mux_4x1_4_out_9));
  Mux_4x1 mux_4x1_5 (
    .I0(1'b0), .I1(A3), .I2(A2), .I3(A1), .S0(S0), .S1(S1), .Y(LSL4), .out_8(mux_4x1_5_out_8),
    .out_9(mux_4x1_5_out_9));
endmodule

module Mux_4x1 (
  input  I0,
  input  I1,
  input  I2,
  input  I3,
  input  S0,
  input  S1,
  output Y,
  output out_8,
  output out_9
);

  wire and_1_out, and_2_out, and_3_out, and_4_out;

  and and_1 (and_1_out, I0, ~S0, ~S1);  // AND_Gate
  and and_2 (and_2_out, I1, S0, ~S1);  // AND_Gate
  and and_3 (and_3_out, I2, ~S0, S1);  // AND_Gate
  and and_4 (and_4_out, I3, S0, S1);
  or or_1 (Y, and_1_out, and_2_out, and_3_out, and_4_out);

  assign out_8 = S0;
  assign out_9 = S1;
endmodule

module Mux_2x1 (
  input  I0,
  input  I1,
  input  S,
  output Y,
  output out_5
);

  wire and_1_out, and_2_out;

  and and_1 (and_1_out, I0, ~S);  // AND_Gate
  and and_2 (and_2_out, I1, S);
  or or_1 (Y, and_1_out, and_2_out);

  assign out_5 = S;
endmodule

module Mux_2x4 (
  input  a0,
  input  b0,
  input  a1,
  input  b1,
  input  a2,
  input  b2,
  input  a3,
  input  b3,
  input  S,
  output y0,
  output y1,
  output y2,
  output y3
);

  wire mux_2x1_2_out_5, mux_2x1_3_out_5, mux_2x1_4_out_5;

  Mux_2x1 mux_2x1_1 (.I0(a0), .I1(b0), .S(mux_2x1_2_out_5), .Y(y0));  // open: out_5
  Mux_2x1 mux_2x1_2 (.I0(a1), .I1(b1), .S(mux_2x1_3_out_5), .Y(y1), .out_5(mux_2x1_2_out_5));
  Mux_2x1 mux_2x1_3 (.I0(a2), .I1(b2), .S(mux_2x1_4_out_5), .Y(y2), .out_5(mux_2x1_3_out_5));
  Mux_2x1 mux_2x1_4 (.I0(a3), .I1(b3), .S(S), .Y(y3), .out_5(mux_2x1_4_out_5));
endmodule

// CT0
module CyBw (
  input  CyBwi,
  input  S0,
  input  S1,
  output C0
);

  wire xor_1_out;

  xor xor_1 (xor_1_out, CyBwi, S0);
  or or_1 (C0, xor_1_out, S1);
endmodule

// BT
module BTrans (
  input  B0,
  input  B1,
  input  B2,
  input  B3,
  input  C,
  output BT0,
  output BT1,
  output BT2,
  output BT3
);

  xor xor_1 (BT0, B0, C);
  xor xor_2 (BT1, B1, C);
  xor xor_3 (BT2, B2, C);
  xor xor_4 (BT3, B3, C);
endmodule

// CT4
module C4T (
  input  C4,
  input  SnA,
  output CyBwA
);

  xor xor_1 (CyBwA, C4, SnA);
endmodule

module main_PAL (
  input  CyBwi,
  input  A3,
  input  in_3,
  input  in_4,
  input  A0,
  input  B3,
  input  in_7,
  input  in_8,
  input  B0,
  input  S2,
  input  S1,
  input  S0,
  output LE,
  output V,
  output CyBwo,
  output R3,
  output out_17,
  output out_18,
  output R0
);

  // PLD pld_1: pin names not known; wires that end beside it: A0, in_4, in_3, A3, B0, in_8, in_7, B3, CyBwi, S0, S1, S2, LE, CyBwo, V, R3, out_17, out_18, R0
endmodule
