// Logisim project LEETC_LSD_Trabalho_3_2023_24.circ as structural Verilog: 7 circuits, main circuit TIME_COUNTER
module LEETC_LSD_Trabalho_3_2023_24 (
  output out_1
);

  wire button_1_out;

  Button button_1 (.out(button_1_out));
  Circuito circuito_1 (.BUTTON(button_1_out), .LAMP(out_1));
endmodule

module Circuito (
  input  BUTTON,
  output LAMP
);

  wire button_counter_1_tc, ctrl_1_reset_time, MCLK_out, OSC_1Hz_out, RST_BUTTON, time_4_1_time_4,
       time_7_1_time_7, time_counter_1_c0, time_counter_1_c1, time_counter_1_c2;

  Clock OSC_1Hz (.out(OSC_1Hz_out));
  Clock MCLK (.out(MCLK_out));
  TIME_COUNTER time_counter_1 (
    .RST(ctrl_1_reset_time), .OSC_1Hz(OSC_1Hz_out), .C0(time_counter_1_c0), .C1(time_counter_1_c1),
    .C2(time_counter_1_c2));
  BUTTON_COUNTER button_counter_1 (.RST(RST_BUTTON), .CLK(BUTTON), .TC(button_counter_1_tc));
  TIME_7 time_7_1 (.C0(time_counter_1_c0), .C1(time_counter_1_c1), .C2(time_counter_1_c2), .TIME_7(time_7_1_time_7));
  TIME_4 time_4_1 (.C0(time_counter_1_c0), .C1(time_counter_1_c1), .C2(time_counter_1_c2), .TIME_4(time_4_1_time_4));
  CTRL ctrl_1 (
    .TIME_LAMP_ON(time_7_1_time_7), .TIME_WINDOW(time_4_1_time_4), .LAMP_FOREVER(button_counter_1_tc),
    .BUTTON(BUTTON), .CLK(MCLK_out), .RESET_TIME(ctrl_1_reset_time), .RST_BUTTON(RST_BUTTON), .LAMP(LAMP));
endmodule

module TIME_COUNTER (
  input  RST,
  input  OSC_1Hz,
  output C0,
  output C1,
  output C2
);
endmodule

module BUTTON_COUNTER (
  input  RST,
  input  CLK,
  output TC
);
endmodule

module CTRL (
  input  TIME_LAMP_ON,
  input  TIME_WINDOW,
  input  LAMP_FOREVER,
  input  BUTTON,
  input  CLK,
  output RESET_TIME,
  output RST_BUTTON,
  output LAMP
);
endmodule

module TIME_7 (
  input  C0,
  input  C1,
  input  C2,
  output TIME_7
);

  and and_1 (TIME_7, C0, C1, C2);
endmodule

module TIME_4 (
  input  C0,
  input  C1,
  input  C2,
  output TIME_4
);

  and and_1 (TIME_4, ~C0, ~C1, C2);  // AND_Gate
endmodule
