// Logisim project logisim_teste_completo.circ as structural Verilog: 1 circuit, main circuit main
module main (
  input  BUTTON,
  output TIME,
  output out_3,
  output out_4,
  output BTN_COUNT,
  output CS,
  output out_7,
  output out_8,
  output LAMP,
  output out_10
);

  wire clock_1_out, OSC_1HZ_out;

  Clock clock_1 (.out(clock_1_out));
  Clock #(.highDuration(500), .lowDuration(500)) OSC_1HZ (.out(OSC_1HZ_out));
  // PLD #(.Contents("{\"version\":\"1.0\",\"deviceId\":\"v750c\",\"file\":\"LEETC_LSD_Trabalho_3_2023_24.doc\",\"variables\":{},\"productTerms\":[{\"type\":\"X\",\"pin\":19,\"name\":\"BTN_COUNT0.t\",\"expression\":\"1\"},{\"type\":\"X\",\"pin\":19,\"name\":\"BTN_COUNT0.ar\",\"expression\":\"!CS0\\u0026!CS1\\u0026!CS2\"},{\"type\":\"X\",\"pin\":19,\"name\":\"BTN_COUNT0.ck\",\"expression\":\"BUTTON\"},{\"type\":\"X\",\"pin\":19,\"name\":\"BTN_COUNT0.sp\",\"expression\":\"0\"},{\"type\":\"X\",\"pin\":20,\"name\":\"BTN_COUNT1.t\",\"expression\":\"BTN_COUNT0\"},{\"type\":\"X\",\"pin\":20,\"name\":\"BTN_COUNT1.ar\",\"expression\":\"!CS0\\u0026!CS1\\u0026!CS2\"},{\"type\":\"X\",\"pin\":20,\"name\":\"BTN_COUNT1.ck\",\"expression\":\"BUTTON\"},{\"type\":\"X\",\"pin\":20,\"name\":\"BTN_COUNT1.sp\",\"expression\":\"0\"},{\"type\":\"X\",\"pin\":16,\"name\":\"CS0.d\",\"expression\":\"!BUTTON\\u0026!CS1#CS0\\u0026CS1\\u0026!CS2\\u0026!TIME0#CS0\\u0026CS1\\u0026!CS2\\u0026!TIME1#CS0\\u0026CS1\\u0026!CS2\\u0026!TIME2#!BTN_COUNT0\\u0026CS1\\u0026!CS2\\u0026!TIME0\\u0026!TIME1\\u0026TIME2#!BTN_COUNT1\\u0026CS1\\u0026!CS2\\u0026!TIME0\\u0026!TIME1\\u0026TIME2\"},{\"type\":\"X\",\"pin\":16,\"name\":\"CS0.ar\",\"expression\":\"0\"},{\"type\":\"X\",\"pin\":16,\"name\":\"CS0.ckmux\",\"expression\":\"MCLK\"},{\"type\":\"X\",\"pin\":16,\"name\":\"CS0.sp\",\"expression\":\"0\"},{\"type\":\"X\",\"pin\":17,\"name\":\"CS1.d\",\"expression\":\"BUTTON\\u0026CS0\\u0026!CS1#BUTTON\\u0026CS0\\u0026!CS2#CS1\\u0026!CS2\\u0026!TIME2#BUTTON\\u0026!CS0\\u0026CS1\\u0026CS2#!BTN_COUNT0\\u0026!CS0\\u0026CS1\\u0026!CS2#!BTN_COUNT1\\u0026!CS0\\u0026CS1\\u0026!CS2#!CS0\\u0026CS1\\u0026!CS2\\u0026TIME0#CS1\\u0026!CS2\\u0026!TIME0\\u0026TIME1#CS0\\u0026CS1\\u0026!CS2\\u0026!TIME1\"},{\"type\":\"X\",\"pin\":17,\"name\":\"CS1.ar\",\"expression\":\"0\"},{\"type\":\"X\",\"pin\":17,\"name\":\"CS1.ckmux\",\"expression\":\"MCLK\"},{\"type\":\"X\",\"pin\":17,\"name\":\"CS1.sp\",\"expression\":\"0\"},{\"type\":\"X\",\"pin\":18,\"name\":\"CS2.d\",\"expression\":\"!CS1\\u0026CS2#BUTTON\\u0026!CS0\\u0026CS2#BUTTON\\u0026CS0\\u0026CS1\\u0026!CS2\\u0026TIME0\\u0026TIME1\\u0026TIME2#BTN_COUNT0\\u0026BTN_COUNT1\\u0026!CS0\\u0026CS1\\u0026!CS2\\u0026!TIME0\\u0026!TIME1\\u0026TIME2\"},{\"type\":\"X\",\"pin\":18,\"name\":\"CS2.ar\",\"expression\":\"0\"},{\"type\":\"X\",\"pin\":18,\"name\":\"CS2.ckmux\",\"expression\":\"MCLK\"},{\"type\":\"X\",\"pin\":18,\"name\":\"CS2.sp\",\"expression\":\"0\"},{\"type\":\"V\",\"pin\":14,\"name\":\"LAMP\",\"expression\":\"!CS1\\u0026CS2#CS1\\u0026!CS2\"},{\"type\":\"I\",\"pin\":0,\"name\":\"LAMP_FOREVER\",\"expression\":\"BTN_COUNT0\\u0026BTN_COUNT1\"},{\"type\":\"I\",\"pin\":0,\"name\":\"RST_BUTTON\",\"expression\":\"!CS0\\u0026!CS1\\u0026!CS2\"},{\"type\":\"I\",\"pin\":0,\"name\":\"RST_TIME\",\"expression\":\"CS0\\u0026!CS1\\u0026!CS2\"},{\"type\":\"X\",\"pin\":21,\"name\":\"TIME0.t\",\"expression\":\"1\"},{\"type\":\"X\",\"pin\":21,\"name\":\"TIME0.ar\",\"expression\":\"CS0\\u0026!CS1\\u0026!CS2\"},{\"type\":\"X\",\"pin\":21,\"name\":\"TIME0.ck\",\"expression\":\"OSC_1HZ\"},{\"type\":\"X\",\"pin\":21,\"name\":\"TIME0.sp\",\"expression\":\"0\"},{\"type\":\"X\",\"pin\":22,\"name\":\"TIME1.t\",\"expression\":\"TIME0\"},{\"type\":\"X\",\"pin\":22,\"name\":\"TIME1.ar\",\"expression\":\"CS0\\u0026!CS1\\u0026!CS2\"},{\"type\":\"X\",\"pin\":22,\"name\":\"TIME1.ck\",\"expression\":\"OSC_1HZ\"},{\"type\":\"X\",\"pin\":22,\"name\":\"TIME1.sp\",\"expression\":\"0\"},{\"type\":\"X\",\"pin\":23,\"name\":\"TIME2.t\",\"expression\":\"TIME0\\u0026TIME1\"},{\"type\":\"X\",\"pin\":23,\"name\":\"TIME2.ar\",\"expression\":\"CS0\\u0026!CS1\\u0026!CS2\"},{\"type\":\"X\",\"pin\":23,\"name\":\"TIME2.ck\",\"expression\":\"OSC_1HZ\"},{\"type\":\"X\",\"pin\":23,\"name\":\"TIME2.sp\",\"expression\":\"0\"},{\"type\":\"I\",\"pin\":0,\"name\":\"TIME_LAMP_ON\",\"expression\":\"TIME0\\u0026TIME1\\u0026TIME2\"},{\"type\":\"I\",\"pin\":0,\"name\":\"TIME_WINDOW\",\"expression\":\"!TIME0\\u0026!TIME1\\u0026TIME2\"},{\"type\":\"D\",\"pin\":19,\"name\":\"BTN_COUNT0.oe\",\"expression\":\"1\"},{\"type\":\"D\",\"pin\":20,\"name\":\"BTN_COUNT1.oe\",\"expression\":\"1\"},{\"type\":\"D\",\"pin\":16,\"name\":\"CS0.oe\",\"expression\":\"1\"},{\"type\":\"D\",\"pin\":17,\"name\":\"CS1.oe\",\"expression\":\"1\"},{\"type\":\"D\",\"pin\":18,\"name\":\"CS2.oe\",\"expression\":\"1\"},{\"type\":\"D\",\"pin\":14,\"name\":\"LAMP.oe\",\"expression\":\"1\"},{\"type\":\"D\",\"pin\":21,\"name\":\"TIME0.oe\",\"expression\":\"1\"},{\"type\":\"D\",\"pin\":22,\"name\":\"TIME1.oe\",\"expression\":\"1\"},{\"type\":\"D\",\"pin\":23,\"name\":\"TIME2.oe\",\"expression\":\"1\"}],\"projectName\":\"LEETC_LSD_Trabalho_3_2023_24\",\"pins\":{\"16\":{\"termUsed\":\"-\",\"type\":\"V\",\"name\":\"CS0\",\"number\":16,\"negated\":false,\"extensions\":{\"ar\":false,\"d\":false,\"oe\":false,\"ckmux\":false,\"sp\":false},\"fuseNot\":false},\"17\":{\"termUsed\":\"-\",\"type\":\"V\",\"name\":\"CS1\",\"number\":17,\"negated\":false,\"extensions\":{\"ar\":false,\"d\":false,\"oe\":false,\"ckmux\":false,\"sp\":false},\"fuseNot\":false},\"1\":{\"termUsed\":\"-\",\"type\":\"V\",\"name\":\"MCLK\",\"number\":1,\"negated\":false,\"extensions\":{},\"fuseNot\":false},\"18\":{\"termUsed\":\"-\",\"type\":\"V\",\"name\":\"CS2\",\"number\":18,\"negated\":false,\"extensions\":{\"ar\":false,\"d\":false,\"oe\":false,\"ckmux\":false,\"sp\":false},\"fuseNot\":false},\"19\":{\"termUsed\":\"-\",\"type\":\"V\",\"name\":\"BTN_COUNT0\",\"number\":19,\"negated\":false,\"extensions\":{\"ar\":false,\"t\":false,\"oe\":false,\"ck\":false,\"sp\":false},\"fuseNot\":false},\"3\":{\"termUsed\":\"-\",\"type\":\"V\",\"name\":\"BUTTON\",\"number\":3,\"negated\":false,\"extensions\":{},\"fuseNot\":false},\"20\":{\"termUsed\":\"-\",\"type\":\"V\",\"name\":\"BTN_COUNT1\",\"number\":20,\"negated\":false,\"extensions\":{\"ar\":false,\"t\":false,\"oe\":false,\"ck\":false,\"sp\":false},\"fuseNot\":false},\"5\":{\"termUsed\":\"-\",\"type\":\"V\",\"name\":\"OSC_1HZ\",\"number\":5,\"negated\":false,\"extensions\":{},\"fuseNot\":false},\"21\":{\"termUsed\":\"-\",\"type\":\"V\",\"name\":\"TIME0\",\"number\":21,\"negated\":false,\"extensions\":{\"ar\":false,\"t\":false,\"oe\":false,\"ck\":false,\"sp\":false},\"fuseNot\":false},\"22\":{\"termUsed\":\"-\",\"type\":\"V\",\"name\":\"TIME1\",\"number\":22,\"negated\":false,\"extensions\":{\"ar\":false,\"t\":false,\"oe\":false,\"ck\":false,\"sp\":false},\"fuseNot\":false},\"23\":{\"termUsed\":\"-\",\"type\":\"V\",\"name\":\"TIME2\",\"number\":23,\"negated\":false,\"extensions\":{\"ar\":false,\"t\":false,\"oe\":false,\"ck\":false,\"sp\":false},\"fuseNot\":false},\"14\":{\"termUsed\":\"2\",\"type\":\"V\",\"name\":\"LAMP\",\"number\":14,\"negated\":false,\"extensions\":{\"oe\":false},\"fuseNot\":false}}}")) pld_1: pin names not known; wires that end beside it: clock_1_out, BUTTON, OSC_1HZ_out, TIME, out_3, out_4, BTN_COUNT, CS, out_7, out_8, out_10, LAMP
endmodule
